# Fritzing sketch circuit (saved by Fritzing 0.9.4)
breadboards: 1

parts:
  R1 = Resistor [tolerance=±5% resistance=330 package="0603 [SMD]"]
  LED1 = LED - 5mm [color="Red (633nm)" package="5 mm [THT]"]
  Raspberry_Pi_1 = Raspberry Pi 3 [part_number=RPI-3-V1.2]
  R2 = Resistor [tolerance=±5% resistance=330 package="0603 [SMD]"]
  LED2 = LED - 5mm [color="Yellow (595nm)" package="5 mm [THT]"]

nets:
  N1: R1.Pin_0, LED1.cathode
  N2: R1.Pin_1, Raspberry_Pi_1.GND, R2.Pin_1
  N3: LED1.anode, Raspberry_Pi_1.GIPO17
  N4: Raspberry_Pi_1.GIPO27, LED2.anode
  N5: R2.Pin_0, LED2.cathode

// code stored in the sketch: IOT_Lab100_NodeMCU_Test.ino
/* -------------------------------------------------------------------
 *  NOTES: DEFAULT pin connection with NodeMCU(ESP8266)
 *  VCC --> 3v3
 *  GND --> GND
 *  SCL --> D1 ( GPIO 5)
 *  SDA --> D2 ( GPIO 4)
 *  RESET --> D4 ( GPIO 2 )  // initialized parameter.
 * ------------------------------------------------------------------
 *  For NodeMCU :
 *  SCL --> D5 ( GPIO 14)
 *  SDA --> D6 ( GPIO 12)
 */
#include <SPI.h>
#include <Wire.h>
#include <Adafruit_GFX.h>
#include <Adafruit_SSD1306.h>

// ---------------------------------------------
// for DHT- 11 讀取溫濕度
#include <dht.h>
#include <TimedAction.h>
// ---------------------------------------------
// ---------------------------------------------
#define DHT11_PIN D7
// ---------------------------------------------
#define OLED_RESET 2
#define OLED_ADDRESS  0x3C
#define OLED_SCL_PIN  D5
#define OLED_SDA_PIN  D6
Adafruit_SSD1306 display(OLED_RESET);

#define NUMFLAKES 10
#define XPOS 0
#define YPOS 1
#define DELTAY 2

void buttonPressHandler();

// http://www.instructables.com/id/Change-Adafruit-Library-OLED-Logo/
//------------------------------------------------------------------------------
// File generated by LCD Assistant
// http://en.radzio.dxp.pl/bitmap_converter/
//------------------------------------------------------------------------------ 
static const unsigned char PROGMEM THE_LOGO [] = {  // 128 * 64
0x00, 0x00, 0x00, 0x00, 0x00, 0x00, 0x00, 0x00, 0x00, 0x00, 0x00, 0x00, 0x00, 0x00, 0x00, 0x00,
0x00, 0x00, 0x00, 0x00, 0x00, 0x00, 0x00, 0x00, 0x00, 0x00, 0x00, 0x00, 0x00, 0x00, 0x00, 0x00,
0x00, 0x00, 0x00, 0x00, 0x00, 0x00, 0x00, 0x00, 0x00, 0x00, 0x00, 0x00, 0x00, 0x00, 0x00, 0x00,
0x00, 0x00, 0x0C, 0x00, 0x00, 0x00, 0x00, 0x00, 0x00, 0x00, 0x00, 0x00, 0x00, 0x00, 0x00, 0x00,
0x00, 0x00, 0x10, 0x00, 0x00, 0x00, 0xE3, 0xC7, 0x87, 0x00, 0x00, 0x00, 0x00, 0x00, 0x00, 0x00,
0x00, 0x00, 0x10, 0x00, 0x00, 0x01, 0x12, 0x64, 0xC8, 0x80, 0x00, 0x00, 0x00, 0x00, 0x00, 0x00,
0x00, 0x00, 0x3D, 0xCE, 0x2D, 0xC0, 0x14, 0x28, 0x40, 0x80, 0x02, 0xC3, 0x91, 0x10, 0x00, 0x00,
0x00, 0x00, 0x11, 0x11, 0x32, 0x40, 0x14, 0x28, 0x40, 0x80, 0x03, 0x24, 0x52, 0x90, 0x00, 0x00,
0x00, 0x00, 0x11, 0x11, 0x22, 0x40, 0x24, 0x28, 0x41, 0x0C, 0x82, 0x24, 0x4A, 0xA0, 0x00, 0x00,
0x00, 0x00, 0x11, 0x11, 0x22, 0x40, 0x44, 0x28, 0x42, 0x13, 0x02, 0x24, 0x4A, 0xA0, 0x00, 0x00,
0x00, 0x00, 0x11, 0x11, 0x22, 0x40, 0x86, 0x4C, 0x84, 0x00, 0x02, 0x24, 0x4C, 0x60, 0x00, 0x00,
0x00, 0x00, 0x11, 0x0E, 0x22, 0x41, 0xF3, 0xC7, 0x8F, 0x80, 0x02, 0x23, 0x84, 0x40, 0x00, 0x00,
0x00, 0x00, 0x00, 0x00, 0x00, 0x00, 0x00, 0x00, 0x00, 0x00, 0x00, 0x00, 0x00, 0x00, 0x00, 0x00,
0x00, 0x00, 0x00, 0x00, 0x00, 0x00, 0x00, 0x00, 0x00, 0x00, 0x00, 0x00, 0x00, 0x00, 0x00, 0x00,
0xFF, 0xFF, 0xFF, 0xFF, 0xFF, 0xFF, 0xFF, 0xFF, 0xFF, 0xFF, 0xFF, 0xFF, 0xFF, 0xFF, 0xFF, 0xFF,
0x00, 0x00, 0x00, 0x00, 0x00, 0x00, 0x00, 0x00, 0x00, 0x00, 0x00, 0x00, 0x00, 0x00, 0x00, 0x00,
0x00, 0x00, 0x00, 0x00, 0x00, 0x00, 0x00, 0x00, 0x00, 0x00, 0x00, 0x00, 0x00, 0x00, 0x00, 0x00,
0x00, 0x00, 0x00, 0x00, 0x00, 0x00, 0x00, 0x00, 0x00, 0x00, 0x00, 0x00, 0x00, 0x00, 0x00, 0x00,
0x00, 0x00, 0x00, 0x00, 0x00, 0x00, 0x00, 0x00, 0x00, 0x00, 0x00, 0x00, 0x00, 0x00, 0x00, 0x00,
0x00, 0x00, 0x00, 0x06, 0x18, 0x00, 0x00, 0x00, 0x00, 0x00, 0x00, 0x00, 0x00, 0x00, 0x00, 0x00,
0x00, 0x00, 0x00, 0x0C, 0x18, 0x01, 0xFF, 0xFF, 0x00, 0x60, 0x30, 0x00, 0x60, 0x00, 0x00, 0x00,
0x00, 0x00, 0x00, 0x0C, 0x3F, 0xE1, 0xFF, 0xFF, 0x0F, 0xF4, 0x30, 0x00, 0x40, 0x00, 0x00, 0x00,
0x00, 0x00, 0x00, 0x0C, 0x7F, 0xE0, 0x01, 0x00, 0x0F, 0x8E, 0x30, 0x00, 0x40, 0x00, 0x00, 0x00,
0x00, 0x00, 0x00, 0x1B, 0xE0, 0xC0, 0x41, 0x06, 0x01, 0x81, 0xB0, 0x00, 0xC0, 0x00, 0x00, 0x00,
0x00, 0x00, 0x00, 0x1B, 0x59, 0x80, 0xE1, 0x06, 0x01, 0x80, 0xB0, 0x7F, 0xFF, 0xE0, 0x00, 0x00,
0x00, 0x00, 0x00, 0x3B, 0x0F, 0x00, 0x61, 0x0C, 0x1F, 0xF0, 0x30, 0x7F, 0xFF, 0xE0, 0x00, 0x00,
0x00, 0x00, 0x00, 0x7B, 0x1F, 0x80, 0x31, 0x1C, 0x1F, 0xFC, 0x30, 0x00, 0xE0, 0x00, 0x00, 0x00,
0x00, 0x00, 0x00, 0x7B, 0xF9, 0xF0, 0x31, 0x18, 0x01, 0xC6, 0x30, 0x00, 0xE0, 0x00, 0x00, 0x00,
0x00, 0x00, 0x00, 0x1B, 0x60, 0x60, 0x01, 0x00, 0x03, 0xC3, 0x30, 0x01, 0xB0, 0x00, 0x00, 0x00,
0x00, 0x00, 0x00, 0x1B, 0x0E, 0x03, 0xFF, 0xFF, 0x83, 0xE1, 0xB0, 0x01, 0xB0, 0x00, 0x00, 0x00,
0x00, 0x00, 0x00, 0x1B, 0x3C, 0x83, 0xFF, 0xFF, 0x87, 0xA0, 0x30, 0x03, 0x18, 0x00, 0x00, 0x00,
0x00, 0x00, 0x00, 0x1B, 0xF3, 0xC0, 0x01, 0x00, 0x0D, 0xA1, 0xFC, 0x03, 0x18, 0x00, 0x00, 0x00,
0x00, 0x00, 0x00, 0x1B, 0x0F, 0x70, 0x01, 0x00, 0x1D, 0x9F, 0xFC, 0x06, 0x0C, 0x00, 0x00, 0x00,
0x00, 0x00, 0x00, 0x1B, 0x7C, 0xE0, 0x01, 0x00, 0x09, 0x8F, 0x30, 0x0C, 0x06, 0x00, 0x00, 0x00,
0x00, 0x00, 0x00, 0x1B, 0x63, 0xC0, 0x01, 0x00, 0x01, 0x80, 0x30, 0x1C, 0x03, 0x00, 0x00, 0x00,
0x00, 0x00, 0x00, 0x1B, 0x0F, 0x00, 0x01, 0x00, 0x01, 0x80, 0x30, 0x78, 0x01, 0xC0, 0x00, 0x00,
0x00, 0x00, 0x00, 0x18, 0xFC, 0x00, 0x01, 0x00, 0x01, 0x80, 0x30, 0xE0, 0x00, 0xE0, 0x00, 0x00,
0x00, 0x00, 0x00, 0x18, 0xE0, 0x00, 0x01, 0x00, 0x01, 0x80, 0x30, 0x40, 0x00, 0x40, 0x00, 0x00,
0x00, 0x00, 0x00, 0x00, 0x00, 0x00, 0x01, 0x00, 0x00, 0x00, 0x00, 0x00, 0x00, 0x00, 0x00, 0x00,
0x00, 0x00, 0x00, 0x00, 0x00, 0x00, 0x00, 0x00, 0x00, 0x00, 0x00, 0x00, 0x00, 0x00, 0x00, 0x00,
0x00, 0x00, 0x00, 0x00, 0x00, 0x00, 0x00, 0x00, 0x00, 0x00, 0x00, 0x00, 0x00, 0x00, 0x00, 0x00,
0x00, 0x00, 0x00, 0x00, 0x00, 0x00, 0x00, 0x00, 0x00, 0x06, 0x08, 0x06, 0x40, 0x00, 0x00, 0x00,
0x00, 0x00, 0x20, 0x04, 0x7E, 0x06, 0x7F, 0x8F, 0x18, 0x06, 0x08, 0x04, 0x57, 0x80, 0x20, 0x00,
0x00, 0x1F, 0x7F, 0x86, 0x22, 0x05, 0x41, 0x89, 0x3F, 0x06, 0x7F, 0x8C, 0x58, 0x00, 0xE0, 0x00,
0x00, 0x00, 0xD9, 0x9F, 0x22, 0x0D, 0xD7, 0x89, 0x73, 0x1F, 0x08, 0x09, 0xF8, 0x07, 0xA0, 0x00,
0x00, 0x00, 0xB9, 0x00, 0x22, 0x0B, 0x55, 0x89, 0x56, 0x06, 0x08, 0x14, 0x40, 0x06, 0x60, 0x00,
0x00, 0x1F, 0x6E, 0x1F, 0x22, 0x1E, 0x5F, 0x8F, 0x1C, 0x06, 0x08, 0x04, 0x47, 0x80, 0xC4, 0x00,
0x00, 0x00, 0xC3, 0x80, 0x7A, 0x06, 0x49, 0x82, 0x3F, 0x07, 0x7F, 0x0D, 0x51, 0x03, 0x9C, 0x00,
0x00, 0x07, 0xFE, 0x1F, 0x22, 0x0D, 0x4D, 0x8A, 0x61, 0x8E, 0x61, 0x0D, 0x51, 0x07, 0xF0, 0x00,
0x00, 0x06, 0x02, 0x00, 0x22, 0x0F, 0x5F, 0x8B, 0x80, 0x1E, 0x23, 0x1D, 0x51, 0x00, 0xE6, 0x00,
0x00, 0x07, 0xFE, 0x1F, 0x22, 0x1D, 0xD1, 0x8A, 0x3F, 0x06, 0x32, 0x1D, 0x51, 0x03, 0x87, 0x00,
0x00, 0x06, 0x02, 0x19, 0x22, 0x80, 0x51, 0x8A, 0x21, 0x06, 0x16, 0x0D, 0x51, 0x0F, 0xF9, 0x00,
0x00, 0x07, 0xFE, 0x19, 0x22, 0x8F, 0x51, 0x8A, 0x21, 0x06, 0x1C, 0x0D, 0x5D, 0x01, 0x6C, 0x00,
0x00, 0x06, 0x02, 0x19, 0x22, 0x8B, 0x5F, 0x8B, 0xA1, 0x06, 0x1E, 0x0F, 0x41, 0x06, 0x67, 0x00,
0x00, 0x07, 0xFE, 0x1F, 0x23, 0x9B, 0x41, 0x8F, 0x3F, 0x06, 0x63, 0x0C, 0x41, 0x18, 0x61, 0x80,
0x00, 0x1F, 0x0F, 0x99, 0x21, 0x10, 0x43, 0x18, 0x21, 0x0C, 0xC1, 0x8C, 0x47, 0x00, 0xE0, 0x00,
0x00, 0x00, 0x00, 0x00, 0x00, 0x00, 0x00, 0x00, 0x00, 0x00, 0x00, 0x00, 0x00, 0x00, 0x00, 0x00,
0x00, 0x00, 0x00, 0x00, 0x00, 0x00, 0x00, 0x00, 0x00, 0x00, 0x00, 0x00, 0x00, 0x00, 0x00, 0x00,
0x00, 0x00, 0x00, 0x00, 0x00, 0x00, 0x00, 0x00, 0x00, 0x00, 0x00, 0x00, 0x00, 0x00, 0x00, 0x00,
0xFF, 0xFF, 0xFF, 0xFF, 0xFF, 0xFF, 0xFF, 0xFF, 0xFF, 0xFF, 0xFF, 0xFF, 0xFF, 0xFF, 0xFF, 0xFF,
0x00, 0x00, 0x00, 0x00, 0x00, 0x00, 0x00, 0x00, 0x00, 0x00, 0x00, 0x00, 0x00, 0x00, 0x00, 0x00,
0x00, 0x00, 0x00, 0x00, 0x00, 0x00, 0x00, 0x00, 0x00, 0x00, 0x00, 0x00, 0x00, 0x00, 0x00, 0x00,
0x00, 0x00, 0x00, 0x00, 0x00, 0x00, 0x00, 0x00, 0x00, 0x00, 0x00, 0x00, 0x00, 0x00, 0x00, 0x00,
0x00, 0x00, 0x00, 0x00, 0x00, 0x00, 0x00, 0x00, 0x00, 0x00, 0x00, 0x00, 0x00, 0x00, 0x00, 0x00
};

#if (SSD1306_LCDHEIGHT != 64)
#error("Height incorrect, please fix Adafruit_SSD1306.h!");
#endif

//
volatile boolean onOff = false;
void buttonPressHandler() {
   Serial.println("Pressed!");
   onOff = !onOff;
   digitalWrite( D1, onOff);   
}

void setup()   {                
  Serial.begin(115200);
  // OLED ---------------------------------------------------
  display.begin(SSD1306_SWITCHCAPVCC, OLED_ADDRESS, OLED_SDA_PIN, OLED_SCL_PIN);  // initialize with the I2C addr 0x3C (for the 128x64) , SDA/SCL
  display.clearDisplay();
  // ---------------------------------------------------------------
  display.drawBitmap(0,0, THE_LOGO, 128, 64, 1);
  display.display();
  delay(2000);
  //display.clearDisplay();
  ESP.wdtFeed();
  //
}

int ledPins[3] = { D1, D2, D4 };
int pinIndex = 0;
//
dht DHT;
void readTH() {
    int temp=0, humi=0;
    int chk = DHT.read11(DHT11_PIN); // Digital
    if(chk == DHTLIB_OK) {
        temp = DHT.temperature;
        humi = DHT.humidity;
    }
    else {
        Serial.print("Random ...");
        // 測試用： 隨機產生 for DEMO Only !!
        temp = 29 + random(-8, 8);
        humi = 70 + random( -20, 20); 
    }
    Serial.print("Temperature = ");
    Serial.print(temp);
    Serial.print(",  Humidity = ");
    Serial.println(humi);
    //
    display.clearDisplay();
    //
    display.setTextSize(1);
    display.setCursor(0,0);
    display.println( millis() );
    display.println( );
    display.setTextSize(2);
    display.print("TEMP:");
    display.println(temp);
    display.print("Humi:");
    display.println(humi);
    //
    display.display();
    
    // 輪流閃燈: D1, D2, D4
    // 全部關閉
    for (int i=0; i<3; i++) {
        pinMode( ledPins[i] , OUTPUT);
        digitalWrite( ledPins[i], LOW);
    }
    // 打開某一個燈號
    digitalWrite( ledPins[pinIndex], HIGH);
    pinIndex = (pinIndex+1) % 3;
    //
} 

TimedAction readTHjob  = TimedAction( 1000, readTH );


void loop() {
   // ready to read 溫溼度 ??
   readTHjob.check(); 
   //
   ESP.wdtFeed();
}

void testdrawchar(void) {
  display.setTextSize(1);
  display.setTextColor(WHITE);
  display.setCursor(0,0);

  for (uint8_t i=0; i < 168; i++) {
    if (i == '\n') continue;
    display.write(i);
    if ((i > 0) && (i % 21 == 0))
      display.println();
  }    
  display.display();
  delay(100);
}

void testdrawline() {  
  for (int16_t i=0; i<display.width(); i+=4) {
    display.drawLine(0, 0, i, display.height()-1, WHITE);
    display.display();
    delay(1);
  }
  for (int16_t i=0; i<display.height(); i+=4) {
    display.drawLine(0, 0, display.width()-1, i, WHITE);
    display.display();
    delay(1);
  }
  delay(250);
}
